// Logisim project 14_Bit_RISC-V_CPU_Datapath_Final.circ as structural Verilog
module _1_Bit_ALU (
  input  Carry_In,
  input  A,
  input  Ainvert,
  input  [1:0] in_4,
  input  B,
  input  Binvert,
  input  Less,
  output R,
  output Set,
  output Carry_Out
);

  wire and_1_out, multiplexer_1_out, multiplexer_2_out, not_1_out, not_2_out, or_1_out;

  not not_1 (not_1_out, A);
  not not_2 (not_2_out, B);
  Multiplexer multiplexer_1 (.in0(A), .in1(not_1_out), .out(multiplexer_1_out), .sel(Ainvert));  // open: en
  Multiplexer multiplexer_2 (.in0(B), .in1(not_2_out), .out(multiplexer_2_out), .sel(Binvert));  // open: en
  and and_1 (and_1_out, multiplexer_1_out, multiplexer_2_out);
  or or_1 (or_1_out, multiplexer_1_out, multiplexer_2_out);
  Adder #(.width(1)) adder_1 (
    .a(multiplexer_1_out), .b(multiplexer_2_out), .out(Set), .cin(Carry_In), .cout(Carry_Out));
  Multiplexer #(.select(2)) multiplexer_3 (
    .in0(and_1_out), .in1(or_1_out), .in2(Set), .in3(Less), .out(R), .sel(in_4));  // open: en
endmodule

module _14_Bit_ALU (
  input  in_1,
  input  [1:0] in_2,
  input  [13:0] B,
  input  [13:0] A,
  input  B_inv,
  input  A_inv,
  output [13:0] out_7,
  output Zero_Signal,
  output Overflow
);

  wire n1_bit_alu_1_carry_out, n1_bit_alu_2_carry_out, n1_bit_alu_3_carry_out, n1_bit_alu_4_carry_out,
       n1_bit_alu_5_carry_out, n1_bit_alu_6_carry_out, n1_bit_alu_7_carry_out, n1_bit_alu_8_carry_out,
       n1_bit_alu_9_carry_out, n1_bit_alu_10_carry_out, n1_bit_alu_11_carry_out, n1_bit_alu_12_carry_out,
       n1_bit_alu_13_carry_out, n1_bit_alu_14_carry_out, n1_bit_alu_14_set;

  _1_Bit_ALU u_1_bit_alu_1 (
    .A(A[0]), .Ainvert(A_inv), .B(B[0]), .Binvert(B_inv), .Less(n1_bit_alu_14_set), .R(out_7[0]),
    .in_4(in_2), .Carry_In(in_1), .Carry_Out(n1_bit_alu_1_carry_out));  // open: Set
  _1_Bit_ALU u_1_bit_alu_2 (
    .A(A[1]), .Ainvert(A_inv), .B(B[1]), .Binvert(B_inv), .Less(1'b0), .R(out_7[1]), .in_4(in_2),
    .Carry_In(n1_bit_alu_1_carry_out), .Carry_Out(n1_bit_alu_2_carry_out));  // open: Set
  _1_Bit_ALU u_1_bit_alu_3 (
    .A(A[2]), .Ainvert(A_inv), .B(B[2]), .Binvert(B_inv), .Less(1'b0), .R(out_7[2]), .in_4(in_2),
    .Carry_In(n1_bit_alu_2_carry_out), .Carry_Out(n1_bit_alu_3_carry_out));  // open: Set
  _1_Bit_ALU u_1_bit_alu_4 (
    .A(A[3]), .Ainvert(A_inv), .B(B[3]), .Binvert(B_inv), .Less(1'b0), .R(out_7[3]), .in_4(in_2),
    .Carry_In(n1_bit_alu_3_carry_out), .Carry_Out(n1_bit_alu_4_carry_out));  // open: Set
  _1_Bit_ALU u_1_bit_alu_5 (
    .A(A[4]), .Ainvert(A_inv), .B(B[4]), .Binvert(B_inv), .Less(1'b0), .R(out_7[4]), .in_4(in_2),
    .Carry_In(n1_bit_alu_4_carry_out), .Carry_Out(n1_bit_alu_5_carry_out));  // open: Set
  _1_Bit_ALU u_1_bit_alu_6 (
    .A(A[5]), .Ainvert(A_inv), .B(B[5]), .Binvert(B_inv), .Less(1'b0), .R(out_7[5]), .in_4(in_2),
    .Carry_In(n1_bit_alu_5_carry_out), .Carry_Out(n1_bit_alu_6_carry_out));  // open: Set
  _1_Bit_ALU u_1_bit_alu_7 (
    .A(A[6]), .Ainvert(A_inv), .B(B[6]), .Binvert(B_inv), .Less(1'b0), .R(out_7[6]), .in_4(in_2),
    .Carry_In(n1_bit_alu_6_carry_out), .Carry_Out(n1_bit_alu_7_carry_out));  // open: Set
  _1_Bit_ALU u_1_bit_alu_8 (
    .A(A[7]), .Ainvert(A_inv), .B(B[7]), .Binvert(B_inv), .Less(1'b0), .R(out_7[7]), .in_4(in_2),
    .Carry_In(n1_bit_alu_7_carry_out), .Carry_Out(n1_bit_alu_8_carry_out));  // open: Set
  _1_Bit_ALU u_1_bit_alu_9 (
    .A(A[8]), .Ainvert(A_inv), .B(B[8]), .Binvert(B_inv), .Less(1'b0), .R(out_7[8]), .in_4(in_2),
    .Carry_In(n1_bit_alu_8_carry_out), .Carry_Out(n1_bit_alu_9_carry_out));  // open: Set
  _1_Bit_ALU u_1_bit_alu_10 (
    .A(A[9]), .Ainvert(A_inv), .B(B[9]), .Binvert(B_inv), .Less(1'b0), .R(out_7[9]), .in_4(in_2),
    .Carry_In(n1_bit_alu_9_carry_out), .Carry_Out(n1_bit_alu_10_carry_out));  // open: Set
  _1_Bit_ALU u_1_bit_alu_11 (
    .A(A[10]), .Ainvert(A_inv), .B(B[10]), .Binvert(B_inv), .Less(1'b0), .R(out_7[10]), .in_4(in_2),
    .Carry_In(n1_bit_alu_10_carry_out), .Carry_Out(n1_bit_alu_11_carry_out));  // open: Set
  _1_Bit_ALU u_1_bit_alu_12 (
    .A(A[11]), .Ainvert(A_inv), .B(B[11]), .Binvert(B_inv), .Less(1'b0), .R(out_7[11]), .in_4(in_2),
    .Carry_In(n1_bit_alu_11_carry_out), .Carry_Out(n1_bit_alu_12_carry_out));  // open: Set
  _1_Bit_ALU u_1_bit_alu_13 (
    .A(A[12]), .Ainvert(A_inv), .B(B[12]), .Binvert(B_inv), .Less(1'b0), .R(out_7[12]), .in_4(in_2),
    .Carry_In(n1_bit_alu_12_carry_out), .Carry_Out(n1_bit_alu_13_carry_out));  // open: Set
  _1_Bit_ALU u_1_bit_alu_14 (
    .A(A[13]), .Ainvert(A_inv), .B(B[13]), .Binvert(B_inv), .Less(1'b0), .R(out_7[13]), .in_4(in_2),
    .Set(n1_bit_alu_14_set), .Carry_In(n1_bit_alu_13_carry_out), .Carry_Out(n1_bit_alu_14_carry_out));
  xor xor_1 (Overflow, n1_bit_alu_13_carry_out, n1_bit_alu_14_carry_out);
  nor nor_1 (Zero_Signal, out_7[0], out_7[1], out_7[2], out_7[3], out_7[4], out_7[5], out_7[6], out_7[7], out_7[8], out_7[9], out_7[10], out_7[11], out_7[12], out_7[13]);
endmodule

module Register_File (
  input  [13:0] Write_Data,
  input  [3:0] RD,
  input  [3:0] RS,
  input  Write_Enable,
  input  Clock,
  output [13:0] Read_1,
  output [13:0] Read_2
);

  wire and_1_out, and_2_out, and_3_out, and_4_out, and_5_out, and_6_out, and_7_out, and_8_out, and_9_out,
       and_10_out, and_11_out, and_12_out, and_13_out, and_14_out, and_15_out, and_16_out, decoder_1_out0,
       decoder_1_out1, decoder_1_out2, decoder_1_out3, decoder_1_out4, decoder_1_out5, decoder_1_out6,
       decoder_1_out7, decoder_1_out8, decoder_1_out9, decoder_1_out10, decoder_1_out11, decoder_1_out12,
       decoder_1_out13, decoder_1_out14, decoder_1_out15;
  wire [13:0] s0_q, s1_q, s2_q, s3_q, s4_q, s5_q, s6_q, s7_q, sp_q, t0_q, t1_q, t2_q, t3_q, t4_q, t5_q,
       zero_q;

  Decoder #(.select(4)) decoder_1 (
    .out0(decoder_1_out0), .out1(decoder_1_out1), .out2(decoder_1_out2), .out3(decoder_1_out3),
    .out4(decoder_1_out4), .out5(decoder_1_out5), .out6(decoder_1_out6), .out7(decoder_1_out7),
    .out8(decoder_1_out8), .out9(decoder_1_out9), .out10(decoder_1_out10), .out11(decoder_1_out11),
    .out12(decoder_1_out12), .out13(decoder_1_out13), .out14(decoder_1_out14), .out15(decoder_1_out15),
    .sel(RD));  // open: en
  and and_1 (and_1_out, decoder_1_out0, Write_Enable);
  and and_2 (and_2_out, decoder_1_out1, Write_Enable);
  and and_3 (and_3_out, decoder_1_out2, Write_Enable);
  and and_4 (and_4_out, decoder_1_out3, Write_Enable);
  and and_5 (and_5_out, decoder_1_out4, Write_Enable);
  and and_6 (and_6_out, decoder_1_out5, Write_Enable);
  and and_7 (and_7_out, decoder_1_out6, Write_Enable);
  and and_8 (and_8_out, decoder_1_out7, Write_Enable);
  and and_9 (and_9_out, decoder_1_out8, Write_Enable);
  and and_10 (and_10_out, decoder_1_out9, Write_Enable);
  and and_11 (and_11_out, decoder_1_out10, Write_Enable);
  and and_12 (and_12_out, decoder_1_out11, Write_Enable);
  and and_13 (and_13_out, decoder_1_out12, Write_Enable);
  and and_14 (and_14_out, decoder_1_out13, Write_Enable);
  and and_15 (and_15_out, decoder_1_out14, Write_Enable);
  and and_16 (and_16_out, decoder_1_out15, Write_Enable);
  Register #(.width(14)) zero (.D(Write_Data), .en(and_1_out), .Q(zero_q), .clk(Clock));  // open: clr
  Register #(.width(14)) sp (.D(Write_Data), .en(and_2_out), .Q(sp_q), .clk(Clock));  // open: clr
  Register #(.width(14)) s0 (.D(Write_Data), .en(and_3_out), .Q(s0_q), .clk(Clock));  // open: clr
  Register #(.width(14)) s1 (.D(Write_Data), .en(and_4_out), .Q(s1_q), .clk(Clock));  // open: clr
  Register #(.width(14)) s2 (.D(Write_Data), .en(and_5_out), .Q(s2_q), .clk(Clock));  // open: clr
  Register #(.width(14)) s3 (.D(Write_Data), .en(and_6_out), .Q(s3_q), .clk(Clock));  // open: clr
  Register #(.width(14)) s4 (.D(Write_Data), .en(and_7_out), .Q(s4_q), .clk(Clock));  // open: clr
  Register #(.width(14)) s5 (.D(Write_Data), .en(and_8_out), .Q(s5_q), .clk(Clock));  // open: clr
  Register #(.width(14)) s6 (.D(Write_Data), .en(and_9_out), .Q(s6_q), .clk(Clock));  // open: clr
  Register #(.width(14)) s7 (.D(Write_Data), .en(and_10_out), .Q(s7_q), .clk(Clock));  // open: clr
  Register #(.width(14)) t0 (.D(Write_Data), .en(and_11_out), .Q(t0_q), .clk(Clock));  // open: clr
  Register #(.width(14)) t1 (.D(Write_Data), .en(and_12_out), .Q(t1_q), .clk(Clock));  // open: clr
  Register #(.width(14)) t2 (.D(Write_Data), .en(and_13_out), .Q(t2_q), .clk(Clock));  // open: clr
  Register #(.width(14)) t3 (.D(Write_Data), .en(and_14_out), .Q(t3_q), .clk(Clock));  // open: clr
  Register #(.width(14)) t4 (.D(Write_Data), .en(and_15_out), .Q(t4_q), .clk(Clock));  // open: clr
  Register #(.width(14)) t5 (.D(Write_Data), .en(and_16_out), .Q(t5_q), .clk(Clock));  // open: clr
  Multiplexer #(.select(4), .width(14)) multiplexer_1 (
    .in0(zero_q), .in1(sp_q), .in2(s0_q), .in3(s1_q), .in4(s2_q), .in5(s3_q), .in6(s4_q), .in7(s5_q),
    .in8(s6_q), .in9(s7_q), .in10(t0_q), .in11(t1_q), .in12(t2_q), .in13(t3_q), .in14(t4_q), .in15(t5_q),
    .out(Read_1), .sel(RS));  // open: en
  Multiplexer #(.select(4), .width(14)) multiplexer_2 (
    .in0(zero_q), .in1(sp_q), .in2(s0_q), .in3(s1_q), .in4(s2_q), .in5(s3_q), .in6(s4_q), .in7(s5_q),
    .in8(s6_q), .in9(s7_q), .in10(t0_q), .in11(t1_q), .in12(t2_q), .in13(t3_q), .in14(t4_q), .in15(t5_q),
    .out(Read_2), .sel(RD));  // open: en
endmodule

module Datapath (
  input  [13:0] Data_In,
  output [9:0] out_2,
  output [3:0] Opcode,
  output [13:0] out_4,
  output [13:0] out_5,
  output [3:0] RS,
  output [3:0] RD,
  output out_8,
  output [1:0] Sa,
  output [13:0] out_10,
  output out_11,
  output out_12,
  output [13:0] out_13,
  output [13:0] out_14,
  output [13:0] out_15
);

  wire and_1_out, and_2_out, clock_1_out, control_unit_1_alusrc, control_unit_1_bqbn, control_unit_1_bqst,
       control_unit_1_din, control_unit_1_wrm, control_unit_2_1_ainv, control_unit_2_1_binv,
       control_unit_2_1_branch, control_unit_2_1_cin, control_unit_2_1_jump, control_unit_2_1_load,
       control_unit_2_1_slti, control_unit_2_1_store, control_unit_2_1_wenbl, multiplexer_7_out, not_1_out;
  wire [1:0] control_unit_1_aluop0, control_unit_1_regdst0, control_unit_1_wsrc0;
  wire [3:0] adder_1_out, bit_extender_1_out, multiplexer_1_out, multiplexer_2_out;
  wire [9:0] adder_1_out_2;
  wire [13:0] bit_extender_2_out, bit_extender_3_out, multiplexer_3_out, multiplexer_4_out,
       multiplexer_5_out, multiplexer_6_out, multiplexer_8_out, multiplexer_9_out, ram_1_data, register_1_q;

  Clock clock_1 (.out(clock_1_out));
  Register #(.width(14)) register_1 (.D(multiplexer_9_out), .Q(register_1_q), .clk(clock_1_out));  // open: en, clr
  Control_Unit control_unit_1 (
    .A3(Opcode[3]), .A2(Opcode[2]), .A1(Opcode[1]), .A0(Opcode[0]), .RegDst1(control_unit_1_regdst0[1]),
    .RegDst0(control_unit_1_regdst0[0]), .ALUsrc(control_unit_1_alusrc), .ALUop1(control_unit_1_aluop0[1]),
    .ALUop0(control_unit_1_aluop0[0]), .BqSt(control_unit_1_bqst), .Wrm(control_unit_1_wrm),
    .Wsrc1(control_unit_1_wsrc0[1]), .Wsrc0(control_unit_1_wsrc0[0]), .BqBn(control_unit_1_bqbn),
    .Din(control_unit_1_din));
  Control_Unit_2 control_unit_2_1 (
    .A3(Opcode[3]), .A2(Opcode[2]), .A1(Opcode[1]), .A0(Opcode[0]), .Wenbl(control_unit_2_1_wenbl),
    .Ainv(control_unit_2_1_ainv), .Binv(control_unit_2_1_binv), .Cin(control_unit_2_1_cin),
    .Load(control_unit_2_1_load), .Store(control_unit_2_1_store), .Branch(control_unit_2_1_branch),
    .Jump(control_unit_2_1_jump), .Slti(control_unit_2_1_slti));
  Multiplexer #(.width(4)) multiplexer_1 (
    .in0(4'b1000), .in1(4'b1001), .out(multiplexer_1_out), .sel(control_unit_1_bqst));  // open: en
  Adder #(.width(14)) adder_1 (.a(register_1_q), .b(14'h1), .out({adder_1_out, adder_1_out_2}));  // open: cin, cout
  ROM #(.addrWidth(14), .dataWidth(14)) rom_1 (.addr(register_1_q), .data({Opcode, out_2}));  // open: sel
  assign bit_extender_1_out = {{2{1'b0}}, out_2[1:0]};  // Bit_Extender bit_extender_1
  Multiplexer #(.select(2), .width(4)) multiplexer_2 (
    .in0(out_2[9:6]), .in1(out_2[5:2]), .in2(multiplexer_1_out), .in3(4'b0001), .out(multiplexer_2_out),
    .sel(control_unit_1_regdst0));  // open: en
  assign bit_extender_2_out = {{8{1'b0}}, out_2[5:0]};  // Bit_Extender bit_extender_2
  Shifter #(.width(14)) shifter_1 (.in(out_5), .\dist (bit_extender_1_out), .out(out_13));
  Shifter #(.width(14), .shift("lr")) shifter_2 (.in(out_5), .\dist (bit_extender_1_out), .out(out_15));
  Register_File register_file_1 (
    .RD(multiplexer_2_out), .Write_Enable(control_unit_2_1_wenbl), .Clock(clock_1_out), .Read_1(out_4),
    .RS(out_2[9:6]), .Write_Data(multiplexer_3_out), .Read_2(out_5));
  Multiplexer #(.width(14)) multiplexer_3 (
    .in0(multiplexer_5_out), .in1(Data_In), .out(multiplexer_3_out), .sel(control_unit_1_din));  // open: en
  Multiplexer #(.width(14)) multiplexer_4 (
    .in0(out_5), .in1(bit_extender_2_out), .out(multiplexer_4_out), .sel(control_unit_1_alusrc));  // open: en
  _14_Bit_ALU u_14_bit_alu_1 (
    .out_7({out_10[13:1], out_8}), .Zero_Signal(out_11), .Overflow(out_12), .B_inv(control_unit_2_1_binv),
    .A_inv(control_unit_2_1_ainv), .B(multiplexer_4_out), .A(out_4), .in_1(control_unit_2_1_cin),
    .in_2(control_unit_1_aluop0));
  not not_1 (not_1_out, out_11);
  Multiplexer #(.select(2), .width(14)) multiplexer_5 (
    .in0(multiplexer_8_out), .in1(out_13), .in2(out_15), .in3(bit_extender_3_out), .out(multiplexer_5_out),
    .sel(control_unit_1_wsrc0));  // open: en
  Multiplexer #(.width(14)) multiplexer_6 (
    .in0({adder_1_out, adder_1_out_2}), .in1(bit_extender_2_out), .out(multiplexer_6_out), .sel(and_1_out));  // open: en
  and and_1 (and_1_out, control_unit_2_1_branch, multiplexer_7_out);
  Multiplexer multiplexer_7 (
    .in0(out_11), .in1(not_1_out), .out(multiplexer_7_out), .sel(control_unit_1_bqbn));  // open: en
  RAM #(.addrWidth(14), .dataWidth(14), .bus("separate")) ram_1 (
    .addr({out_10[13:1], out_8}), .din(out_5), .data(ram_1_data), .str(control_unit_2_1_store),
    .clk(clock_1_out), .ld(control_unit_2_1_load));  // open: sel, clr
  Multiplexer #(.width(14)) multiplexer_8 (
    .in0({out_10[13:1], out_8}), .in1(ram_1_data), .out(multiplexer_8_out), .sel(control_unit_1_wrm));  // open: en
  Multiplexer #(.width(14)) multiplexer_9 (
    .in0(multiplexer_6_out), .in1({adder_1_out, out_2}), .out(multiplexer_9_out), .sel(control_unit_2_1_jump));  // open: en
  and and_2 (and_2_out, control_unit_2_1_slti, out_8);
  assign bit_extender_3_out = {{13{1'b0}}, and_2_out};  // Bit_Extender bit_extender_3

  assign out_10[0] = out_8;
  assign out_14 = out_5;
  assign RD = out_2[5:2];
  assign RS = out_2[9:6];
  assign Sa = out_2[1:0];

  // Notes on the sheet:
  //   contents of rom_1 (hex, n*v repeats v):
  //   14c 594 e1c 1260 3814 3c14 1660 1823 1c23 3104 3588 9c5 21c5 25c6 2983 2c02
endmodule

module Control_Unit (
  input  A3,
  input  A2,
  input  A1,
  input  A0,
  output RegDst1,
  output RegDst0,
  output ALUsrc,
  output ALUop1,
  output ALUop0,
  output BqSt,
  output Wrm,
  output Wsrc1,
  output Wsrc0,
  output BqBn,
  output Din
);

  wire and_1_out, and_2_out, and_3_out, and_4_out, and_5_out, and_6_out, and_7_out, and_8_out, and_9_out,
       and_10_out, and_11_out, and_14_out, and_15_out, and_16_out, and_17_out, not_1_out, not_2_out,
       not_3_out, not_4_out, not_5_out, not_6_out, not_7_out, not_8_out, not_9_out, not_10_out, not_11_out,
       not_12_out, not_13_out, not_14_out, not_15_out, not_16_out, not_17_out, not_18_out, not_19_out,
       not_20_out, not_21_out, not_22_out, not_23_out, not_24_out, not_25_out, not_26_out, not_27_out,
       not_28_out, not_29_out, not_30_out, not_31_out, not_32_out, not_33_out;

  and and_1 (and_1_out, A3, not_1_out, not_2_out);
  not not_1 (not_1_out, A2);
  not not_2 (not_2_out, A0);
  and and_2 (and_2_out, A3, not_3_out);
  not not_3 (not_3_out, A1);
  not not_4 (not_4_out, A3);
  and and_3 (and_3_out, not_4_out, not_5_out);
  not not_5 (not_5_out, A1);
  not not_6 (not_6_out, A3);
  and and_4 (and_4_out, not_6_out, A0);
  not not_7 (not_7_out, A2);
  and and_5 (and_5_out, not_7_out, A1, not_8_out);
  not not_8 (not_8_out, A0);
  and and_6 (and_6_out, A3, A2, not_9_out);
  not not_9 (not_9_out, A1);
  not not_10 (not_10_out, A2);
  and and_7 (and_7_out, not_10_out, not_11_out);
  not not_11 (not_11_out, A1);
  not not_12 (not_12_out, A2);
  and and_8 (and_8_out, not_12_out, not_13_out);
  not not_13 (not_13_out, A0);
  and and_9 (and_9_out, A3, not_14_out);
  not not_14 (not_14_out, A1);
  not not_15 (not_15_out, A3);
  not not_16 (not_16_out, A1);
  not not_17 (not_17_out, A0);
  not not_18 (not_18_out, A2);
  not not_19 (not_19_out, A0);
  not not_20 (not_20_out, A2);
  not not_21 (not_21_out, A0);
  not not_22 (not_22_out, A1);
  not not_23 (not_23_out, A0);
  not not_24 (not_24_out, A3);
  not not_25 (not_25_out, A2);
  not not_26 (not_26_out, A0);
  not not_27 (not_27_out, A3);
  not not_28 (not_28_out, A0);
  not not_29 (not_29_out, A2);
  not not_30 (not_30_out, A0);
  not not_31 (not_31_out, A2);
  not not_32 (not_32_out, A1);
  not not_33 (not_33_out, A0);
  or or_1 (RegDst1, and_1_out, and_2_out);
  or or_2 (RegDst0, and_3_out, and_4_out, A2);
  or or_3 (ALUsrc, and_5_out, and_6_out);
  or or_4 (ALUop1, and_7_out, and_8_out, and_9_out);
  and and_10 (and_10_out, not_15_out, A2, not_16_out, not_17_out);
  or or_5 (ALUop0, and_10_out, and_11_out);
  and and_11 (and_11_out, A3, not_18_out, A1, not_19_out);
  and and_12 (BqSt, A3, not_20_out, A1, not_21_out);
  and and_13 (Wrm, A3, A2, not_22_out, not_23_out);
  and and_14 (and_14_out, not_24_out, A2, A1, A0);
  or or_6 (Wsrc1, and_14_out, and_15_out);
  and and_15 (and_15_out, A3, not_25_out, A1, not_26_out);
  and and_16 (and_16_out, not_27_out, A2, A1, not_28_out);
  or or_7 (Wsrc0, and_16_out, and_17_out);
  and and_17 (and_17_out, A3, not_29_out, A1, not_30_out);
  and and_18 (BqBn, A3, not_31_out, not_32_out, A0);
  and and_19 (Din, A3, A2, A1, not_33_out);
endmodule

module Control_Unit_2 (
  input  A3,
  input  A2,
  input  A1,
  input  A0,
  output Wenbl,
  output Ainv,
  output Binv,
  output Cin,
  output Load,
  output Store,
  output Branch,
  output Jump,
  output Slti
);

  wire and_1_out, and_2_out, and_3_out, and_4_out, and_5_out, and_6_out, and_7_out, not_1_out, not_2_out,
       not_3_out, not_4_out, not_5_out, not_6_out, not_7_out, not_8_out, not_9_out, not_10_out, not_11_out,
       not_12_out, not_13_out, not_14_out, not_15_out, not_16_out, not_17_out, not_18_out, not_19_out,
       not_20_out, not_21_out, not_22_out, not_23_out;

  not not_1 (not_1_out, A3);
  and and_1 (and_1_out, A1, not_2_out);
  not not_2 (not_2_out, A0);
  and and_2 (and_2_out, A2, not_3_out);
  not not_3 (not_3_out, A0);
  not not_4 (not_4_out, A3);
  not not_5 (not_5_out, A1);
  not not_6 (not_6_out, A3);
  not not_7 (not_7_out, A1);
  and and_3 (and_3_out, not_6_out, not_7_out, A0);
  not not_8 (not_8_out, A2);
  and and_4 (and_4_out, A3, not_8_out, not_9_out);
  not not_9 (not_9_out, A1);
  not not_10 (not_10_out, A2);
  and and_5 (and_5_out, A3, not_10_out, not_11_out);
  not not_11 (not_11_out, A0);
  not not_12 (not_12_out, A2);
  and and_6 (and_6_out, not_12_out, not_13_out, A0);
  not not_13 (not_13_out, A1);
  and and_7 (and_7_out, A3, not_14_out, not_15_out);
  not not_14 (not_14_out, A2);
  not not_15 (not_15_out, A0);
  not not_16 (not_16_out, A1);
  not not_17 (not_17_out, A0);
  not not_18 (not_18_out, A1);
  and and_8 (Branch, A3, not_19_out, not_20_out);
  not not_19 (not_19_out, A2);
  not not_20 (not_20_out, A1);
  not not_21 (not_21_out, A2);
  not not_22 (not_22_out, A2);
  not not_23 (not_23_out, A0);
  or or_1 (Wenbl, not_1_out, and_1_out, and_2_out);
  and and_9 (Ainv, not_4_out, A2, not_5_out, A0);
  or or_2 (Binv, and_3_out, and_4_out, and_5_out);
  or or_3 (Cin, and_6_out, and_7_out);
  and and_10 (Load, A3, A2, not_16_out, not_17_out);
  and and_11 (Store, A3, A2, not_18_out, A0);
  and and_12 (Jump, A3, not_21_out, A1, A0);
  and and_13 (Slti, A3, not_22_out, A1, not_23_out);
endmodule
